// Logisim project H2.circ as structural Verilog: 2 circuits, main circuit P2
module P2 (
  input  S1,
  input  S0,
  input  In,
  output S1n,
  output S0n,
  output Out
);

  wire and_1_out, and_2_out, and_3_out, and_4_out, and_5_out, and_6_out, and_7_out, and_8_out;

  and and_1 (and_1_out, ~In, ~S0, ~S1);  // AND_Gate
  and and_2 (and_2_out, ~In, S0, S1);  // AND_Gate
  and and_3 (and_3_out, In, ~S0, S1);  // AND_Gate
  and and_4 (and_4_out, ~In, ~S0, S1);  // AND_Gate
  and and_5 (and_5_out, In, S0, ~S1);  // AND_Gate
  and and_6 (and_6_out, ~In, S0, ~S1);  // AND_Gate
  and and_7 (and_7_out, In, ~S0, ~S1);  // AND_Gate
  and and_8 (and_8_out, In, S0, S1);
  or or_1 (S1n, and_1_out, and_4_out, and_2_out);
  or or_2 (S0n, and_7_out, and_5_out, and_4_out);
  or or_3 (Out, and_7_out, and_6_out, and_4_out, and_2_out, and_8_out);

  // Notes on the sheet:
  //   PROBLEM 2: IMPLEMENTING A STATE TABLE
  //   INPUT SECTION: Do not change anything here!
  //   You may only change the values of the inputs for testing using the hand tool.
  //   Do not introduce any other input or output pins in the circuit.
  //   To your logic
  //   OUTPUT SECTION: Do not change anything here!
  //   Do not introduce any other input or output pins in the circuit.
  //   From your logic
endmodule

module P3 (
  input  In,
  output Out
);

  wire and_5_out, and_6_out, clock_1_out, or_1_out, or_2_out, or_3_out, S0_q, S1_q, S2_q;

  // AND_Gate and_1 has open pins: in0=S2_q, in1=S1_q, in2=S0_q, in3=In, out=open
  // AND_Gate and_2 has open pins: in0=S2_q, in1=S1_q, in2=S0_q, in3=In, out=open
  // AND_Gate and_3 has open pins: in0=S2_q, in1=S1_q, in2=S0_q, in3=In, out=open
  // AND_Gate and_4 has open pins: in0=S2_q, in1=S1_q, in2=S0_q, in3=In, out=open
  // OR_Gate or_1 has open pins: out=or_1_out
  // OR_Gate or_2 has open pins: out=or_2_out
  // OR_Gate or_3 has open pins: out=or_3_out
  Clock clock_1 (.out(clock_1_out));
  D_Flip_Flop S2 (.clk(clock_1_out), .D(or_1_out), .Q(S2_q));  // open: Qn, preset, en, reset
  D_Flip_Flop S1 (.clk(clock_1_out), .D(or_2_out), .Q(S1_q));  // open: Qn, preset, en, reset
  D_Flip_Flop S0 (.clk(clock_1_out), .D(or_3_out), .Q(S0_q));  // open: Qn, preset, en, reset
  or or_4 (Out, and_5_out, and_6_out);
  and and_5 (and_5_out, S2_q, ~S1_q, ~S0_q, ~In);  // AND_Gate
  and and_6 (and_6_out, ~S2_q, ~S1_q, ~S0_q, In);  // AND_Gate

  // Notes on the sheet:
  //   PROBLEM 3: IMPLEMENTING A STATE MACHINE
  //   INPUT SECTION: Do not change anything here!
  //   You may only change the values of the inputs for testing using the hand tool.
  //   Do not introduce any other input or output pins in the circuit.
  //   To your logic
  //   ERm very lost
  //   Just can't figure out how to implement the first part of the ciruit
  //   OUTPUT SECTION: Do not change anything here!
  //   Do not introduce any other input or output pins in the circuit.
  //   From your logic
endmodule
