// Logisim project eLC-3.circ as structural Verilog: 2 circuits, main circuit eLC-3
module eLC_3 (
);

  wire and_2_out, CLOCK, e0, e1, e2, e3, e4, e5, e6, e7, GateALU, GateMDR, GateOFFSET, GatePC, GateREG,
       LD_CC, LD_IR, LD_MAR, LD_MDR, LD_PC, LD_REG, MEM_EN, MEM_RW, MIO_EN, not_1_out, not_2_out, PCMUX,
       SR2MUX;
  wire [1:0] ALUK;
  wire [2:0] CC_q, comparator_1_gt, IR_2_0, IR_8_6, IR_11_9, SR1;
  wire [3:0] OPCODE;
  wire [4:3] IR_4_0;
  wire [5:5] PCOFF;
  wire [15:0] adder_1_out, adder_2_out, adder_3_out, and_1_out, bit_extender_1_out, bit_extender_2_out,
       controlled_buffer_1_out, MAR_q, MDR_q, multiplexer_1_out, multiplexer_2_out, multiplexer_3_out,
       multiplexer_4_out, multiplexer_5_out, multiplexer_6_out, not_3_out, PC_q, R0, R1, R2, R3, R4, R5, R6,
       R7, ram_1_data;

  assign controlled_buffer_1_out = GateOFFSET ? adder_1_out : 16'bz;  // Controlled_Buffer controlled_buffer_1
  Multiplexer #(.width(16), .enable("false")) multiplexer_1 (
    .in0(adder_1_out), .in1(adder_2_out), .out(multiplexer_1_out), .sel(PCMUX));
  Adder #(.width(16)) adder_1 (.a(bit_extender_1_out), .b(PC_q), .out(adder_1_out), .cin(1'b0));  // open: cout
  assign bit_extender_1_out = {{7{IR_8_6[2]}}, {IR_8_6, PCOFF[5], IR_4_0, IR_2_0}};  // Bit_Extender bit_extender_1
  Register #(.width(16)) IR (
    .D(controlled_buffer_1_out), .en(LD_IR), .Q({OPCODE, IR_11_9, IR_8_6, PCOFF[5], IR_4_0, IR_2_0}),
    .clk(CLOCK));  // open: clr
  Multiplexer #(.width(16), .enable("false")) multiplexer_2 (
    .in0(controlled_buffer_1_out), .in1(ram_1_data), .out(multiplexer_2_out), .sel(MIO_EN));
  assign controlled_buffer_1_out = GatePC ? PC_q : 16'bz;  // Controlled_Buffer controlled_buffer_2
  Register #(.width(16)) PC (.D(multiplexer_1_out), .en(LD_PC), .Q(PC_q), .clk(CLOCK));  // open: clr
  assign controlled_buffer_1_out = GateMDR ? MDR_q : 16'bz;  // Controlled_Buffer controlled_buffer_3
  Register #(.width(16)) MDR (.D(multiplexer_2_out), .en(LD_MDR), .Q(MDR_q), .clk(CLOCK));  // open: clr
  Adder #(.width(16)) adder_2 (.a(PC_q), .b(16'h1), .out(adder_2_out), .cin(1'b0));  // open: cout
  Comparator #(.width(16)) comparator_1 (
    .a(controlled_buffer_1_out), .b({16{1'b0}}), .gt(comparator_1_gt[0]), .eq(comparator_1_gt[1]),
    .lt(comparator_1_gt[2]));
  Clock clock_1 (.out(CLOCK));
  Register #(.width(3)) CC (.D(comparator_1_gt), .en(LD_CC), .Q(CC_q), .clk(CLOCK));  // open: clr
  RAM #(.addrWidth(16), .dataWidth(16), .bus("separate")) ram_1 (
    .addr(MAR_q), .din(MDR_q), .data(ram_1_data), .str(MEM_RW), .sel(MEM_EN), .clk(CLOCK), .ld(not_1_out));  // open: clr
  not not_1 (not_1_out, MEM_RW);
  Demultiplexer #(.select(3), .disabled(0)) demultiplexer_1 (
    .out0(e0), .out1(e1), .out2(e2), .out3(e3), .out4(e4), .out5(e5), .out6(e6), .out7(e7), .in(1'b1),
    .sel(IR_11_9), .en(LD_REG));
  Controller FSM (
    .CLOCK(CLOCK), .IR({OPCODE, IR_11_9, IR_8_6, PCOFF[5], IR_4_0, IR_2_0}), .CC(CC_q), .ALUK(ALUK),
    .GateALU(GateALU), .GateMDR(GateMDR), .GateOFFSET(GateOFFSET), .GatePC(GatePC), .GateREG(GateREG),
    .LD_CC(LD_CC), .LD_IR(LD_IR), .LD_MAR(LD_MAR), .LD_MDR(LD_MDR), .LD_REG(LD_REG), .LD_PC(LD_PC),
    .MEM_EN(MEM_EN), .MEM_RW(MEM_RW), .MIO_EN(MIO_EN), .PCMUX(PCMUX), .SR2MUX(SR2MUX));
  Register #(.width(16)) MAR (.D(controlled_buffer_1_out), .en(LD_MAR), .Q(MAR_q), .clk(CLOCK));  // open: clr
  Register #(.width(16)) u_R0 (.D(controlled_buffer_1_out), .en(e0), .Q(R0), .clk(CLOCK));  // open: clr
  Register #(.width(16)) u_R4 (.D(controlled_buffer_1_out), .en(e4), .Q(R4), .clk(CLOCK));  // open: clr
  Multiplexer #(.select(3), .width(16), .enable("false")) multiplexer_3 (
    .in0(R0), .in1(R1), .in2(R2), .in3(R3), .in4(R4), .in5(R5), .in6(R6), .in7(R7), .out(multiplexer_3_out),
    .sel(IR_2_0));
  assign bit_extender_2_out = {{11{IR_4_0[4]}}, {IR_4_0, IR_2_0}};  // Bit_Extender bit_extender_2
  not not_2 (not_2_out, SR2MUX);
  Multiplexer #(.width(16), .enable("false")) multiplexer_4 (
    .in0(bit_extender_2_out), .in1(multiplexer_3_out), .out(multiplexer_4_out), .sel(not_2_out));
  // Probe on multiplexer_4_out
  Register #(.width(16)) u_R1 (.D(controlled_buffer_1_out), .en(e1), .Q(R1), .clk(CLOCK));  // open: clr
  Register #(.width(16)) u_R5 (.D(controlled_buffer_1_out), .en(e5), .Q(R5), .clk(CLOCK));  // open: clr
  Adder #(.width(16)) adder_3 (
    .a(multiplexer_5_out), .b(multiplexer_4_out), .out(adder_3_out), .cin(1'b0));  // open: cout
  assign and_1_out = multiplexer_5_out & multiplexer_4_out;  // AND_Gate and_1, 16 bits wide
  assign not_3_out = ~multiplexer_5_out;  // NOT_Gate not_3, 16 bits wide
  Register #(.width(16)) u_R2 (.D(controlled_buffer_1_out), .en(e2), .Q(R2), .clk(CLOCK));  // open: clr
  Register #(.width(16)) u_R6 (.D(controlled_buffer_1_out), .en(e6), .Q(R6), .clk(CLOCK));  // open: clr
  Multiplexer #(.select(3), .width(16), .enable("false")) multiplexer_5 (
    .in0(R0), .in1(R1), .in2(R2), .in3(R3), .in4(R4), .in5(R5), .in6(R6), .in7(R7), .out(multiplexer_5_out),
    .sel(SR1));
  // Probe on multiplexer_5_out
  Multiplexer #(.select(2), .width(16), .enable("false")) multiplexer_6 (
    .in0(adder_3_out), .in1(and_1_out), .in2(not_3_out), .out(multiplexer_6_out), .sel(ALUK));  // open: in3
  assign controlled_buffer_1_out = GateALU ? multiplexer_6_out : 16'bz;  // Controlled_Buffer controlled_buffer_4
  Register #(.width(16)) u_R3 (.D(controlled_buffer_1_out), .en(e3), .Q(R3), .clk(CLOCK));  // open: clr
  Register #(.width(16)) u_R7 (.D(controlled_buffer_1_out), .en(e7), .Q(R7), .clk(CLOCK));  // open: clr
  assign controlled_buffer_1_out = GateREG ? multiplexer_5_out : 16'bz;  // Controlled_Buffer GateREG
  and and_2 (and_2_out, OPCODE[0], OPCODE[1], ~OPCODE[2], ~OPCODE[3]);  // AND_Gate
  // Probe on controlled_buffer_1_out
  Multiplexer #(.width(3), .enable("false")) multiplexer_7 (.in0(IR_8_6), .in1(IR_11_9), .out(SR1), .sel(and_2_out));

  // Other names for the same wires on the sheet: IR_4_0[2:0] = IR_2_0; PCOFF (some bits) = {IR_8_6, IR_4_0, IR_2_0}

  // Notes on the sheet:
  //   eLC-3 DATAPATH
  //   INPUT SECTION: Do not change anything here!
  //   To test, load a file into memory and tick the clock.
  //   MEMORY
  //   REG FILE
  //   ALU
  //   LOGIC FOR SR1
endmodule

module Controller (
  input  CLOCK,
  input  [15:0] IR,
  input  [2:0] CC,
  output [1:0] ALUK,
  output GateALU,
  output GateMDR,
  output GateOFFSET,
  output GatePC,
  output GateREG,
  output LD_CC,
  output LD_IR,
  output LD_MAR,
  output LD_MDR,
  output LD_REG,
  output LD_PC,
  output MEM_EN,
  output MEM_RW,
  output MIO_EN,
  output PCMUX,
  output SR2MUX
);

  wire _1, _2, _3, _4, _5, _6, _7, _8, _9, _10, _11, _12, _13, _14, _15, _16, ADDI_4_p10, ADDS_4_p10,
       ANDI_4_p10, ANDS_4_p10, BR_nHit_p11, BRHit_4_p11, LD_4_p10, LD_5_p7, LD_6_p10, NOT_4_p10, NOT_4_p11,
       S0, S0n_out, S1, S1n_out, S2, S2n_out, ST_4_p10, ST_5_p9, ST_6_p9, undriven, undriven_2, undriven_3,
       undriven_4, undriven_5, undriven_6, undriven_7, undriven_8, undriven_9, undriven_10, undriven_11,
       undriven_12, undriven_13, undriven_14, undriven_15, undriven_16, undriven_17, undriven_18,
       undriven_19, undriven_20, undriven_21, undriven_22, undriven_23, undriven_24, undriven_25,
       undriven_26, undriven_27, undriven_28, undriven_29, undriven_30, undriven_31, undriven_32,
       undriven_33, undriven_34, undriven_35, undriven_36, undriven_37, undriven_38, undriven_39,
       undriven_40, undriven_41, undriven_42, undriven_43, undriven_44, undriven_45, undriven_46,
       undriven_47, undriven_48, undriven_49, undriven_50, undriven_51, undriven_52, undriven_53,
       undriven_54, undriven_55, undriven_56, undriven_57, undriven_58, undriven_59, undriven_60,
       undriven_61, undriven_62, undriven_63, undriven_64, undriven_65, undriven_66, undriven_67,
       undriven_68, undriven_69, undriven_70, undriven_71, undriven_72, undriven_73, undriven_74,
       undriven_75, undriven_76, undriven_77, undriven_78, undriven_79, undriven_80, undriven_81,
       undriven_82, undriven_83, undriven_84, undriven_85, undriven_86, undriven_87, undriven_88,
       undriven_89, undriven_90, undriven_91, undriven_92, undriven_93, undriven_94, undriven_95,
       undriven_96, undriven_97, undriven_98, undriven_99, undriven_100, undriven_101, undriven_102,
       undriven_103, undriven_104, undriven_105, undriven_106, undriven_107;

  buf Fetch_1 (_1, undriven);  // AND_Gate
  buf Fetch_2 (_2, undriven_2);  // AND_Gate
  buf Fetch_3 (_3, NOT_4_p10);  // AND_Gate
  // AND_Gate NOT_4: pin names not known; wires that end beside it: S0, IR[15], IR[14], IR[13], IR[12], S2, S1, S0, IR[15], NOT_4_p10, NOT_4_p11, _4
  // AND_Gate ADDS_4: pin names not known; wires that end beside it: IR[15], IR[14], IR[13], IR[12], S2, S1, S0, IR[15], NOT_4_p11, ADDS_4_p10, _5
  // AND_Gate ADDI_4: pin names not known; wires that end beside it: IR[15], IR[14], IR[13], IR[12], S2, S1, S0, IR[15], ADDS_4_p10, ADDI_4_p10, _6
  // AND_Gate ANDS_4: pin names not known; wires that end beside it: IR[15], IR[14], IR[13], IR[12], S2, S1, S0, IR[15], ADDI_4_p10, ANDS_4_p10, _7
  // AND_Gate ANDI_4: pin names not known; wires that end beside it: IR[15], IR[14], IR[13], IR[12], S2, S1, S0, IR[15], ANDS_4_p10, ANDI_4_p10, _8
  // AND_Gate LD_4: pin names not known; wires that end beside it: IR[15], IR[14], IR[13], IR[12], S2, S1, S0, IR[15], ANDI_4_p10, LD_4_p10, _9
  // AND_Gate LD_5: pin names not known; wires that end beside it: IR[15], IR[14], IR[13], IR[12], IR[15], LD_4_p10, LD_5_p7, _10
  // AND_Gate LD_6: pin names not known; wires that end beside it: IR[15], IR[14], IR[13], IR[12], S2, S1, S0, IR[15], LD_5_p7, LD_6_p10, _11
  // AND_Gate BRHit_4: pin names not known; wires that end beside it: IR[15], IR[14], IR[13], IR[12], S2, S1, S0, IR[15], IR[14], LD_6_p10, BRHit_4_p11, _12
  // AND_Gate BR_nHit: pin names not known; wires that end beside it: S0, IR[15], IR[14], IR[13], IR[12], S2, S1, S0, IR[15], BRHit_4_p11, BR_nHit_p11, _13
  // AND_Gate ST_4: pin names not known; wires that end beside it: IR[15], IR[14], IR[13], IR[12], S2, S1, S0, IR[15], BR_nHit_p11, ST_4_p10, _14
  // AND_Gate ST_5: pin names not known; wires that end beside it: IR[15], IR[14], IR[13], IR[12], S2, S1, S0, IR[15], ST_5_p9, _15
  // AND_Gate ST_6: pin names not known; wires that end beside it: IR[15], IR[14], IR[13], IR[12], S2, S1, S0, ST_5_p9, ST_6_p9, _16
  or S2n (S2n_out, undriven_3, undriven_4, undriven_5, undriven_11, undriven_12);
  or or_1 (MIO_EN, undriven_6, undriven_13, undriven_18, undriven_23, undriven_28);
  or or_2 (GateMDR, undriven_7, undriven_14, undriven_19, undriven_24, undriven_29);
  or or_3 (PCMUX, undriven_8, undriven_15, undriven_20, undriven_25, undriven_30);
  or or_4 (ALUK[1], undriven_9, undriven_16, undriven_21, undriven_26, undriven_31);
  or or_5 (LD_CC, undriven_10, undriven_17, undriven_22, undriven_27, undriven_32);
  D_Flip_Flop u_S2 (.clk(CLOCK), .D(S2n_out), .Q(S2));  // open: Qn, preset, en, reset
  D_Flip_Flop u_S1 (.clk(CLOCK), .D(S1n_out), .Q(S1));  // open: Qn, preset, en, reset
  D_Flip_Flop u_S0 (.clk(CLOCK), .D(S0n_out), .Q(S0));  // open: Qn, preset, en, reset
  or S1n (S1n_out, undriven_33, undriven_34, undriven_35, undriven_41, undriven_42);
  or or_6 (MEM_RW, undriven_36, undriven_43, undriven_48, undriven_53, undriven_58);
  or or_7 (LD_MAR, undriven_37, undriven_44, undriven_49, undriven_54, undriven_59);
  or or_8 (LD_PC, undriven_38, undriven_45, undriven_50, undriven_55, undriven_60);
  or or_9 (ALUK[0], undriven_39, undriven_46, undriven_51, undriven_56, undriven_61);
  or or_10 (LD_REG, undriven_40, undriven_47, undriven_52, undriven_57, undriven_62);
  or S0n (S0n_out, undriven_63, undriven_64, undriven_65, undriven_71, undriven_72);
  or or_11 (MEM_EN, undriven_66, undriven_73, undriven_78, undriven_83, undriven_88);
  or or_12 (LD_MDR, undriven_67, undriven_74, undriven_79, undriven_84, undriven_89);
  or or_13 (GatePC, undriven_68, undriven_75, undriven_80, undriven_85, undriven_90);
  or or_14 (SR2MUX, undriven_69, undriven_76, undriven_81, undriven_86, undriven_91);
  or or_15 (GateREG, undriven_70, undriven_77, undriven_82, undriven_87, undriven_92);
  or or_16 (GateOFFSET, undriven_93, undriven_96, undriven_99, undriven_102, undriven_105);
  or or_17 (GateALU, undriven_94, undriven_97, undriven_100, undriven_103, undriven_106);
  or or_18 (LD_IR, undriven_95, undriven_98, undriven_101, undriven_104, undriven_107);

  // Other names for the same wires on the sheet: ALUKL = ALUK[0]; ALUKM = ALUK[1]; GateOFF = GateOFFSET

  // Notes on the sheet:
  //   eLC-3 CONTROLLER
  //   INPUT SECTION: Do not change anything here!
  //   You may only change the values of the inputs for testing using the hand tool.
  //   Do not introduce a clock or any other input or output pins in the circuit.
  //   NZP
  //   To your logic
  //   OUTPUT SECTION: Do not change anything here!
  //   Do not introduce a clock any other input or output pins in the circuit.
  //   From your logic
endmodule
